// Logisim project CPU.circ as structural Verilog: 9 circuits, main circuit 1b LU
module _1b_LU (
  input  [1:0] S,
  input  A,
  input  B,
  output F
);

  wire and_1_out, nor_1_out, or_1_out, xor_1_out;

  and and_1 (and_1_out, A, B);
  or or_1 (or_1_out, A, B);
  xor xor_1 (xor_1_out, A, B);
  nor nor_1 (nor_1_out, A, B);
  Multiplexer #(.select(2)) multiplexer_1 (
    .in0(and_1_out), .in1(or_1_out), .in2(xor_1_out), .in3(nor_1_out), .out(F), .sel(S));  // open: en
endmodule

module _4b_AU (
  input  Cin,
  input  Sub,
  input  [3:0] A,
  input  [3:0] B,
  output [3:0] F,
  output Cout
);

  wire [3:0] xor_1_out;

  xor xor_1 (xor_1_out[0], Sub, B[0]);
  xor xor_2 (xor_1_out[1], Sub, B[1]);
  xor xor_3 (xor_1_out[2], Sub, B[2]);
  xor xor_4 (xor_1_out[3], Sub, B[3]);
  Adder #(.width(4)) adder_1 (.a(A), .b(xor_1_out), .out(F), .cin(Cin), .cout(Cout));
endmodule

module _4b_ALU__old_Zero (
  input  [1:0] S,
  input  M,
  input  [3:0] A,
  input  [3:0] B,
  input  Cin,
  input  Less,
  output [3:0] F,
  output Zero,
  output Cout,
  output Overflow,
  output Set
);

  wire decoder_1_out3, decoder_1_out6, decoder_1_out8, decoder_1_out13, n1b_lu_1_f, n1b_lu_2_f, n1b_lu_3_f,
       n1b_lu_4_f;
  wire [2:0] n4b_au_1_f_2;
  wire [3:3] n4b_au_1_f;

  _1b_LU u_1b_lu_1 (.A(A[0]), .B(B[0]), .F(n1b_lu_1_f), .S(S));
  _1b_LU u_1b_lu_2 (.A(A[1]), .B(B[1]), .F(n1b_lu_2_f), .S(S));
  _1b_LU u_1b_lu_3 (.A(A[2]), .B(B[2]), .F(n1b_lu_3_f), .S(S));
  _1b_LU u_1b_lu_4 (.A(A[3]), .B(B[3]), .F(n1b_lu_4_f), .S(S));
  Multiplexer #(.select(2)) multiplexer_1 (
    .in0(n1b_lu_1_f), .in1(n1b_lu_1_f), .in2(n4b_au_1_f_2[0]), .in3(Less), .out(F[0]), .sel({M, S[1]}));  // open: en
  Multiplexer #(.select(2)) multiplexer_2 (
    .in0(n1b_lu_2_f), .in1(n1b_lu_2_f), .in2(n4b_au_1_f_2[1]), .in3(1'b0), .out(F[1]), .sel({M, S[1]}));  // open: en
  Multiplexer #(.select(2)) multiplexer_3 (
    .in0(n1b_lu_3_f), .in1(n1b_lu_3_f), .in2(n4b_au_1_f_2[2]), .in3(1'b0), .out(F[2]), .sel({M, S[1]}));  // open: en
  Multiplexer #(.select(2)) multiplexer_4 (
    .in0(n1b_lu_4_f), .in1(n1b_lu_4_f), .in2(n4b_au_1_f[3]), .in3(1'b0), .out(F[3]), .sel({M, S[1]}));  // open: en
  Decoder #(.select(4)) decoder_1 (
    .out3(decoder_1_out3), .out6(decoder_1_out6), .out8(decoder_1_out8), .out13(decoder_1_out13),
    .sel({n4b_au_1_f[3], B[3], A[3], S[0]}));  // open: out0, out1, out2, out4, out5, out7, out9, out10, out11, out12, out14, out15, en
  nor nor_1 (Zero, F[0], F[1], F[2], F[3]);
  _4b_AU u_4b_au_1 (.A(A), .B(B), .F({n4b_au_1_f[3], n4b_au_1_f_2}), .Cin(Cin), .Cout(Cout), .Sub(S[0]));
  or or_1 (Overflow, decoder_1_out3, decoder_1_out6, decoder_1_out8, decoder_1_out13);
  xor xor_1 (Set, Overflow, n4b_au_1_f[3]);
endmodule

module _4b_ALU (
  input  [1:0] S,
  input  M,
  input  [3:0] A,
  input  [3:0] B,
  input  Cin,
  input  Less,
  output Zero,
  output [3:0] F,
  output Cout,
  output Overflow,
  output Set
);

  wire decoder_1_out3, decoder_1_out6, decoder_1_out8, decoder_1_out13, n1b_lu_1_f, n1b_lu_2_f, n1b_lu_3_f,
       n1b_lu_4_f;
  wire [2:0] n4b_au_1_f_2;
  wire [3:3] n4b_au_1_f;

  nor nor_1 (Zero, A[0], A[1], A[2], A[3]);
  _1b_LU u_1b_lu_1 (.A(A[0]), .B(B[0]), .F(n1b_lu_1_f), .S(S));
  _1b_LU u_1b_lu_2 (.A(A[1]), .B(B[1]), .F(n1b_lu_2_f), .S(S));
  _1b_LU u_1b_lu_3 (.A(A[2]), .B(B[2]), .F(n1b_lu_3_f), .S(S));
  _1b_LU u_1b_lu_4 (.A(A[3]), .B(B[3]), .F(n1b_lu_4_f), .S(S));
  Multiplexer #(.select(2)) multiplexer_1 (
    .in0(n1b_lu_1_f), .in1(n1b_lu_1_f), .in2(n4b_au_1_f_2[0]), .in3(Less), .out(F[0]), .sel({M, S[1]}));  // open: en
  Multiplexer #(.select(2)) multiplexer_2 (
    .in0(n1b_lu_2_f), .in1(n1b_lu_2_f), .in2(n4b_au_1_f_2[1]), .in3(1'b0), .out(F[1]), .sel({M, S[1]}));  // open: en
  Multiplexer #(.select(2)) multiplexer_3 (
    .in0(n1b_lu_3_f), .in1(n1b_lu_3_f), .in2(n4b_au_1_f_2[2]), .in3(1'b0), .out(F[2]), .sel({M, S[1]}));  // open: en
  Multiplexer #(.select(2)) multiplexer_4 (
    .in0(n1b_lu_4_f), .in1(n1b_lu_4_f), .in2(n4b_au_1_f[3]), .in3(1'b0), .out(F[3]), .sel({M, S[1]}));  // open: en
  Decoder #(.select(4)) decoder_1 (
    .out3(decoder_1_out3), .out6(decoder_1_out6), .out8(decoder_1_out8), .out13(decoder_1_out13),
    .sel({n4b_au_1_f[3], B[3], A[3], S[0]}));  // open: out0, out1, out2, out4, out5, out7, out9, out10, out11, out12, out14, out15, en
  _4b_AU u_4b_au_1 (.A(A), .B(B), .F({n4b_au_1_f[3], n4b_au_1_f_2}), .Cin(Cin), .Cout(Cout), .Sub(S[0]));
  or or_1 (Overflow, decoder_1_out3, decoder_1_out6, decoder_1_out8, decoder_1_out13);
  xor xor_1 (Set, Overflow, n4b_au_1_f[3]);
endmodule

module _8b_ALU (
  input  [1:0] Sel,
  input  M,
  input  [7:0] A,
  input  [7:0] B,
  output [7:0] F,
  output Zero,
  output Overflow,
  output Cout
);

  wire n4b_alu_1_cout, n4b_alu_1_zero, n4b_alu_2_set, n4b_alu_2_zero;

  _4b_ALU u_4b_alu_1 (
    .A(A[3:0]), .B(B[3:0]), .F(F[3:0]), .S(Sel), .M(M), .Less(n4b_alu_2_set), .Cout(n4b_alu_1_cout),
    .Cin(Sel[0]), .Zero(n4b_alu_1_zero));  // open: Set, Overflow
  _4b_ALU u_4b_alu_2 (
    .A(A[7:4]), .B(B[7:4]), .F(F[7:4]), .S(Sel), .M(M), .Less(1'b0), .Set(n4b_alu_2_set), .Cout(Cout),
    .Cin(n4b_alu_1_cout), .Zero(n4b_alu_2_zero), .Overflow(Overflow));
  and and_1 (Zero, n4b_alu_1_zero, n4b_alu_2_zero);
endmodule

module _4b_Register (
  input  [3:0] D,
  input  Clock,
  input  Preset,
  input  Enable,
  input  Clear,
  output [3:0] Q
);

  D_Flip_Flop d_ff_1 (.clk(Clock), .D(D[0]), .Q(Q[0]), .preset(Preset), .en(Enable), .reset(Clear));  // open: Qn
  D_Flip_Flop d_ff_2 (.clk(Clock), .D(D[1]), .Q(Q[1]), .preset(Preset), .en(Enable), .reset(Clear));  // open: Qn
  D_Flip_Flop d_ff_3 (.clk(Clock), .D(D[2]), .Q(Q[2]), .preset(Preset), .en(Enable), .reset(Clear));  // open: Qn
  D_Flip_Flop d_ff_4 (.clk(Clock), .D(D[3]), .Q(Q[3]), .preset(Preset), .en(Enable), .reset(Clear));  // open: Qn
endmodule

module _8b_Register (
  input  [7:0] D,
  input  Clock,
  input  Preset,
  input  Enable,
  input  Clear,
  output [7:0] Q
);

  _4b_Register u_4b_register_1 (.D(D[3:0]), .Clock(Clock), .Q(Q[3:0]), .Preset(Preset), .Enable(Enable), .Clear(Clear));
  _4b_Register u_4b_register_2 (.D(D[7:4]), .Clock(Clock), .Q(Q[7:4]), .Preset(Preset), .Enable(Enable), .Clear(Clear));
endmodule

module _8b_CPU (
  input  [11:0] InstOpr,
  input  Clock,
  output [7:0] PC,
  output [7:0] Acc
);

  wire and_1_out, and_2_out, controlled_inverter_1_out, decoder_1_out1, decoder_1_out2, decoder_1_out3,
       decoder_1_out4, decoder_1_out5, decoder_1_out6, decoder_1_out7, decoder_1_out8, decoder_1_out9,
       decoder_1_out10, decoder_1_out11, decoder_1_out12, decoder_1_out13, decoder_1_out14, decoder_1_out15,
       n8b_alu_1_zero, not_1_out, or_1_out, or_3_out, or_5_out, or_6_out, or_9_out;
  wire [1:0] or_4_out, or_8_out;
  wire [7:0] multiplexer_1_out, multiplexer_2_out, multiplexer_3_out, n8b_alu_1_f, ram_1_data;

  or or_1 (or_1_out, decoder_1_out15, decoder_1_out10);
  Multiplexer #(.width(8)) multiplexer_1 (
    .in0(InstOpr[7:0]), .in1(ram_1_data), .out(multiplexer_1_out), .sel(or_1_out));  // open: en
  or or_2 (or_4_out[1], decoder_1_out8, decoder_1_out11);
  or or_3 (or_3_out, decoder_1_out10, or_6_out, decoder_1_out9);
  Counter counter_1 (
    .load(or_3_out), .D(multiplexer_1_out), .count(not_1_out), .Q(PC), .clk(Clock));  // open: carry, clr
  not not_1 (not_1_out, or_3_out);
  or or_4 (or_4_out[0], decoder_1_out6, decoder_1_out11);
  Multiplexer #(.select(2), .width(8)) multiplexer_2 (
    .in0(n8b_alu_1_f), .in1(InstOpr[7:0]), .in2(ram_1_data), .in3(Acc), .out(multiplexer_2_out),
    .sel(or_4_out));  // open: en
  _8b_Register u_8b_register_1 (.D(multiplexer_2_out), .Clock(Clock), .Q(Acc));  // open: Preset, Enable, Clear
  or or_5 (or_5_out, decoder_1_out12, decoder_1_out7, decoder_1_out13);
  Multiplexer #(.width(8)) multiplexer_3 (
    .in0(InstOpr[7:0]), .in1(ram_1_data), .out(multiplexer_3_out), .sel(or_5_out));  // open: en
  and and_1 (and_1_out, n8b_alu_1_zero, decoder_1_out14);
  or or_6 (or_6_out, and_1_out, and_2_out);
  Decoder #(.select(4)) decoder_1 (
    .out1(decoder_1_out1), .out2(decoder_1_out2), .out3(decoder_1_out3), .out4(decoder_1_out4),
    .out5(decoder_1_out5), .out6(decoder_1_out6), .out7(decoder_1_out7), .out8(decoder_1_out8),
    .out9(decoder_1_out9), .out10(decoder_1_out10), .out11(decoder_1_out11), .out12(decoder_1_out12),
    .out13(decoder_1_out13), .out14(decoder_1_out14), .out15(decoder_1_out15), .sel(InstOpr[11:8]));  // open: out0, en
  or or_7 (or_8_out[1], decoder_1_out7, decoder_1_out3, decoder_1_out2);
  and and_2 (and_2_out, n8b_alu_1_zero, decoder_1_out15);
  or or_8 (or_8_out[0], decoder_1_out7, decoder_1_out5, decoder_1_out13, decoder_1_out3, decoder_1_out1);
  or or_9 (or_9_out, decoder_1_out7, decoder_1_out13, decoder_1_out5, decoder_1_out12, decoder_1_out4);
  // Probe on n8b_alu_1_f
  _8b_ALU u_8b_alu_1 (
    .A(Acc), .B(multiplexer_3_out), .F(n8b_alu_1_f), .Zero(n8b_alu_1_zero), .Sel(or_8_out), .M(or_9_out));  // open: Cout, Overflow
  RAM #(.bus("asynch")) ram_1 (
    .addr(InstOpr[7:0]), .data(ram_1_data), .ld(controlled_inverter_1_out));  // open: sel, clr
  assign controlled_inverter_1_out = Clock ? ~decoder_1_out11 : 1'bz;  // Controlled_Inverter controlled_inverter_1
  assign ram_1_data = decoder_1_out11 ? Acc : 8'bz;  // Controlled_Buffer controlled_buffer_1
  // Probe on ram_1_data
endmodule

module Computer (
  output [7:0] out_1
);

  wire clock_1_out, not_1_out;
  wire [3:0] n4b_register_1_q;
  wire [7:0] n8b_cpu_1_pc, n8b_register_1_q;
  wire [11:0] rom_1_data;

  ROM #(.dataWidth(12)) rom_1 (.addr(n8b_cpu_1_pc), .data(rom_1_data));  // open: sel
  // Probe on n8b_register_1_q
  _8b_Register u_8b_register_1 (
    .D(rom_1_data[7:0]), .Clock(not_1_out), .Q(n8b_register_1_q));  // open: Preset, Enable, Clear
  _4b_Register u_4b_register_1 (
    .D(rom_1_data[11:8]), .Clock(not_1_out), .Q(n4b_register_1_q));  // open: Preset, Enable, Clear
  not not_1 (not_1_out, clock_1_out);
  // Probe on n4b_register_1_q
  Clock clock_1 (.out(clock_1_out));
  _8b_CPU u_8b_cpu_1 (
    .InstOpr({n4b_register_1_q, n8b_register_1_q}), .Clock(clock_1_out), .PC(n8b_cpu_1_pc), .Acc(out_1));

  // Notes on the sheet:
  //   contents of rom_1 (hex, n*v repeats v):
  //   0 601 b00 602 b01 800 c01 b02
endmodule
